# Fritzing sketch buzzer (saved by Fritzing 0.8.7b)
breadboards: 1

parts:
  Composant1 = Arduino Uno (Rev3)
  J1 = Piezo Speaker
  R1 = Resistor [tolerance=±10% resistance=260 package=THT]

nets:
  N1: Composant1.D9_PWM, R1.Pin_1
  N2: Composant1.GND, J1.pin1
  N3: J1.pin2, R1.Pin_0
